// Logisim project 8-bit-CPU-design.circ as structural Verilog: 6 circuits, main circuit main
module main (
  input  OE8,
  input  [3:0] OE_Testing_Data2,
  input  Counter_OE,
  input  WE5,
  input  Count_Enable,
  input  OE3,
  input  WE7,
  input  [7:0] Testing_Data,
  input  OE7,
  input  OE_Testing_Data,
  input  Internal_OE,
  input  WE4,
  input  OE2,
  input  WE6,
  input  OE4,
  input  WE1,
  input  WE3,
  input  OE1,
  input  OE5,
  input  WE2,
  output [3:0] MAR_Content,
  output [3:0] out_22,
  output [7:0] IR_Content,
  output [7:0] MBR_Content,
  output [7:0] Reg_A_Content,
  output [7:0] ALU_Result,
  output [7:0] out_27,
  output [7:0] Reg_B_Content
);

  wire clock_1_out;
  wire [3:0] controlled_buffer_1_out, decimal_decode_1_dout, decimal_decode_1_dout_2,
       decimal_decode_1_dout_3, decimal_decode_1_dout_5, decimal_decode_1_dout_6, decimal_decode_1_dout_7,
       decimal_decode_2_dout, decimal_decode_2_dout_2, decimal_decode_2_dout_3, decimal_decode_2_dout_5,
       decimal_decode_2_dout_6, decimal_decode_2_dout_7, mar_1_dout;
  wire [7:0] alu_1_dout, bit_extender_1_out, Instruction_Register_dout;
  wire [31:0] decimal_decode_3_dout, decimal_decode_4_dout, decimal_decode_5_dout;
  wire [31:12] decimal_decode_1_dout_4, decimal_decode_2_dout_4;

  Clock clock_1 (.out(clock_1_out));
  Counter #(.max('h3), .width(4)) counter_1 (
    .count(Count_Enable), .clk(clock_1_out), .D(controlled_buffer_1_out), .Q(out_22));  // open: clr, load, up, carry
  Register Instruction_Register (
    .Clock(clock_1_out), .WE(WE4), .Din(alu_1_dout), .OE(OE2), .Dout(Instruction_Register_dout),
    .Stored_Data(IR_Content));
  Register Register_A (.Clock(clock_1_out), .WE(WE1), .Din(alu_1_dout), .Stored_Data(Reg_A_Content));  // open: OE, Dout
  Register Register_B (.Clock(clock_1_out), .WE(WE2), .Din(alu_1_dout), .Stored_Data(Reg_B_Content));  // open: OE, Dout
  Decimal_Decode decimal_decode_1 (
    .Din(Reg_A_Content),
    .Dout({decimal_decode_1_dout_4[31:28], decimal_decode_1_dout_7, decimal_decode_1_dout_6, decimal_decode_1_dout_5, decimal_decode_1_dout_4[15:12], decimal_decode_1_dout_3, decimal_decode_1_dout_2, decimal_decode_1_dout}));
  ALU alu_1 (
    .Reg_A(Reg_A_Content), .Reg_B(Reg_B_Content), .OE(OE5), .Dout(alu_1_dout), .ALU_Result(ALU_Result));  // open: Carry_Out
  _7_Segment_Display u_7_segment_display_1 (
    .g(decimal_decode_2_dout_4[15]), .f(decimal_decode_2_dout_4[14]), .a(decimal_decode_2_dout_4[13]),
    .b(decimal_decode_2_dout_4[12]), .e(decimal_decode_2_dout_4[31]), .d(decimal_decode_2_dout_4[30]),
    .c(decimal_decode_2_dout_4[29]), .dp(decimal_decode_2_dout_4[28]));
  Decimal_Decode decimal_decode_2 (
    .Din(Reg_B_Content),
    .Dout({decimal_decode_2_dout_4[31:28], decimal_decode_2_dout_7, decimal_decode_2_dout_6, decimal_decode_2_dout_5, decimal_decode_2_dout_4[15:12], decimal_decode_2_dout_3, decimal_decode_2_dout_2, decimal_decode_2_dout}));
  assign controlled_buffer_1_out = Counter_OE ? out_22 : 4'bz;  // Controlled_Buffer controlled_buffer_1
  _7_Segment_Display u_7_segment_display_2 (
    .g(decimal_decode_1_dout_3[3]), .f(decimal_decode_1_dout_3[2]), .a(decimal_decode_1_dout_3[1]),
    .b(decimal_decode_1_dout_3[0]), .e(decimal_decode_1_dout_7[3]), .d(decimal_decode_1_dout_7[2]),
    .c(decimal_decode_1_dout_7[1]), .dp(decimal_decode_1_dout_7[0]));
  _7_Segment_Display u_7_segment_display_3 (
    .g(decimal_decode_1_dout_4[15]), .f(decimal_decode_1_dout_4[14]), .a(decimal_decode_1_dout_4[13]),
    .b(decimal_decode_1_dout_4[12]), .e(decimal_decode_1_dout_4[31]), .d(decimal_decode_1_dout_4[30]),
    .c(decimal_decode_1_dout_4[29]), .dp(decimal_decode_1_dout_4[28]));
  _7_Segment_Display u_7_segment_display_4 (
    .g(decimal_decode_2_dout_2[3]), .f(decimal_decode_2_dout_2[2]), .a(decimal_decode_2_dout_2[1]),
    .b(decimal_decode_2_dout_2[0]), .e(decimal_decode_2_dout_6[3]), .d(decimal_decode_2_dout_6[2]),
    .c(decimal_decode_2_dout_6[1]), .dp(decimal_decode_2_dout_6[0]));
  _7_Segment_Display u_7_segment_display_5 (
    .g(decimal_decode_2_dout_3[3]), .f(decimal_decode_2_dout_3[2]), .a(decimal_decode_2_dout_3[1]),
    .b(decimal_decode_2_dout_3[0]), .e(decimal_decode_2_dout_7[3]), .d(decimal_decode_2_dout_7[2]),
    .c(decimal_decode_2_dout_7[1]), .dp(decimal_decode_2_dout_7[0]));
  Decimal_Decode decimal_decode_3 (.Dout(decimal_decode_3_dout));  // open: Din
  assign bit_extender_1_out = {{4{out_22[3]}}, out_22};  // Bit_Extender bit_extender_1
  _7_Segment_Display u_7_segment_display_6 (
    .g(decimal_decode_1_dout_2[3]), .f(decimal_decode_1_dout_2[2]), .a(decimal_decode_1_dout_2[1]),
    .b(decimal_decode_1_dout_2[0]), .e(decimal_decode_1_dout_6[3]), .d(decimal_decode_1_dout_6[2]),
    .c(decimal_decode_1_dout_6[1]), .dp(decimal_decode_1_dout_6[0]));
  _7_Segment_Display u_7_segment_display_7 (
    .g(decimal_decode_1_dout[3]), .f(decimal_decode_1_dout[2]), .a(decimal_decode_1_dout[1]),
    .b(decimal_decode_1_dout[0]), .e(decimal_decode_1_dout_5[3]), .d(decimal_decode_1_dout_5[2]),
    .c(decimal_decode_1_dout_5[1]), .dp(decimal_decode_1_dout_5[0]));
  _7_Segment_Display u_7_segment_display_8 (
    .g(decimal_decode_2_dout[3]), .f(decimal_decode_2_dout[2]), .a(decimal_decode_2_dout[1]),
    .b(decimal_decode_2_dout[0]), .e(decimal_decode_2_dout_5[3]), .d(decimal_decode_2_dout_5[2]),
    .c(decimal_decode_2_dout_5[1]), .dp(decimal_decode_2_dout_5[0]));
  _7_Segment_Display u_7_segment_display_9 (
    .g(decimal_decode_3_dout[3]), .f(decimal_decode_3_dout[2]), .a(decimal_decode_3_dout[1]),
    .b(decimal_decode_3_dout[0]), .e(decimal_decode_3_dout[19]), .d(decimal_decode_3_dout[18]),
    .c(decimal_decode_3_dout[17]), .dp(decimal_decode_3_dout[16]));
  Decimal_Decode decimal_decode_4 (.Din(bit_extender_1_out), .Dout(decimal_decode_4_dout));
  _7_Segment_Display u_7_segment_display_10 (
    .g(decimal_decode_4_dout[3]), .f(decimal_decode_4_dout[2]), .a(decimal_decode_4_dout[1]),
    .b(decimal_decode_4_dout[0]), .e(decimal_decode_4_dout[19]), .d(decimal_decode_4_dout[18]),
    .c(decimal_decode_4_dout[17]), .dp(decimal_decode_4_dout[16]));
  BitSelector #(.group(4)) bitselector_1 (.in(Instruction_Register_dout), .out(controlled_buffer_1_out), .sel(1'b0));
  LED D7 (.in(alu_1_dout[7]));
  LED D6 (.in(alu_1_dout[6]));
  LED D5 (.in(alu_1_dout[5]));
  LED D4 (.in(alu_1_dout[4]));
  assign alu_1_dout = OE_Testing_Data ? Testing_Data : 8'bz;  // Controlled_Buffer controlled_buffer_2
  LED D3 (.in(alu_1_dout[3]));
  LED D2 (.in(alu_1_dout[2]));
  LED D1 (.in(alu_1_dout[1]));
  LED D0 (.in(alu_1_dout[0]));
  assign alu_1_dout = Internal_OE ? MBR_Content : 8'bz;  // Controlled_Buffer controlled_buffer_3
  Register register_1 (
    .Clock(clock_1_out), .WE(WE6), .Din(alu_1_dout), .OE(OE4), .Dout(alu_1_dout), .Stored_Data(MBR_Content));
  Register register_2 (
    .Clock(clock_1_out), .WE(WE3), .Din(alu_1_dout), .OE(OE1), .Dout(alu_1_dout), .Stored_Data(out_27));
  MAR mar_1 (
    .Clock(clock_1_out), .WE(WE5), .Din(controlled_buffer_1_out), .OE(OE3), .Dout(mar_1_dout),
    .Stored_Data(MAR_Content));
  _7_Segment_Display u_7_segment_display_11 (
    .g(decimal_decode_5_dout[15]), .f(decimal_decode_5_dout[14]), .a(decimal_decode_5_dout[13]),
    .b(decimal_decode_5_dout[12]), .e(decimal_decode_5_dout[31]), .d(decimal_decode_5_dout[30]),
    .c(decimal_decode_5_dout[29]), .dp(decimal_decode_5_dout[28]));
  Decimal_Decode decimal_decode_5 (.Din(out_27), .Dout(decimal_decode_5_dout));
  assign mar_1_dout = OE8 ? OE_Testing_Data2 : 4'bz;  // Controlled_Buffer controlled_buffer_4
  _7_Segment_Display u_7_segment_display_12 (
    .g(decimal_decode_5_dout[11]), .f(decimal_decode_5_dout[10]), .a(decimal_decode_5_dout[9]),
    .b(decimal_decode_5_dout[8]), .e(decimal_decode_5_dout[27]), .d(decimal_decode_5_dout[26]),
    .c(decimal_decode_5_dout[25]), .dp(decimal_decode_5_dout[24]));
  _7_Segment_Display u_7_segment_display_13 (
    .g(decimal_decode_5_dout[7]), .f(decimal_decode_5_dout[6]), .a(decimal_decode_5_dout[5]),
    .b(decimal_decode_5_dout[4]), .e(decimal_decode_5_dout[23]), .d(decimal_decode_5_dout[22]),
    .c(decimal_decode_5_dout[21]), .dp(decimal_decode_5_dout[20]));
  _7_Segment_Display u_7_segment_display_14 (
    .g(decimal_decode_5_dout[3]), .f(decimal_decode_5_dout[2]), .a(decimal_decode_5_dout[1]),
    .b(decimal_decode_5_dout[0]), .e(decimal_decode_5_dout[19]), .d(decimal_decode_5_dout[18]),
    .c(decimal_decode_5_dout[17]), .dp(decimal_decode_5_dout[16]));
  LED ED7 (.in(alu_1_dout[7]));
  LED ED6 (.in(alu_1_dout[6]));
  LED ED5 (.in(alu_1_dout[5]));
  LED ED4 (.in(alu_1_dout[4]));
  LED ED3 (.in(alu_1_dout[3]));
  LED ED2 (.in(alu_1_dout[2]));
  LED ED1 (.in(alu_1_dout[1]));
  LED ED0 (.in(alu_1_dout[0]));
  RAM #(.addrWidth(4)) ram_1 (
    .addr(mar_1_dout), .we(WE7), .oe(OE7), .clk(clock_1_out), .din(alu_1_dout), .dout(alu_1_dout));

  // Notes on the sheet:
  //   Program_Counter
  //   Content_Of_Counter
  //   Internal_Adress_Bus_(4_bits)
  //   Internal_Data_Bus
  //   MBR
  //   Output_Register
  //   MAR
  //   External_Adress_Bus_(4_bits)
  //   External_Data_Bus
endmodule

module Memory (
  input  Clock,
  input  WE,
  input  Din,
  input  OE,
  input  Reset,
  output Dout,
  output Stored_Data
);

  wire and_1_out, and_2_out, not_1_out, or_1_out;

  not not_1 (not_1_out, WE);
  and and_1 (and_1_out, Stored_Data, not_1_out);
  and and_2 (and_2_out, WE, Din);
  D_Flip_Flop d_ff_1 (.D(or_1_out), .clk(Clock), .Q(Stored_Data), .reset(Reset));  // open: Qn, preset
  or or_1 (or_1_out, and_1_out, and_2_out);
  assign Dout = OE ? Stored_Data : 1'bz;  // Controlled_Buffer controlled_buffer_1
endmodule

module Register (
  input  Clock,
  input  WE,
  input  [7:0] Din,
  input  OE,
  output [7:0] Dout,
  output [7:0] Stored_Data
);

  Memory _0 (
    .Clock(Clock), .WE(WE), .Din(Din[0]), .OE(OE), .Dout(Dout[0]), .Stored_Data(Stored_Data[0]));  // open: Reset
  Memory _1 (
    .Clock(Clock), .WE(WE), .Din(Din[1]), .OE(OE), .Dout(Dout[1]), .Stored_Data(Stored_Data[1]));  // open: Reset
  Memory _2 (
    .Clock(Clock), .WE(WE), .Din(Din[2]), .OE(OE), .Dout(Dout[2]), .Stored_Data(Stored_Data[2]));  // open: Reset
  Memory _3 (
    .Clock(Clock), .WE(WE), .Din(Din[3]), .OE(OE), .Dout(Dout[3]), .Stored_Data(Stored_Data[3]));  // open: Reset
  Memory _4 (
    .Clock(Clock), .WE(WE), .Din(Din[4]), .OE(OE), .Dout(Dout[4]), .Stored_Data(Stored_Data[4]));  // open: Reset
  Memory _5 (
    .Clock(Clock), .WE(WE), .Din(Din[5]), .OE(OE), .Dout(Dout[5]), .Stored_Data(Stored_Data[5]));  // open: Reset
  Memory _6 (
    .Clock(Clock), .WE(WE), .Din(Din[6]), .OE(OE), .Dout(Dout[6]), .Stored_Data(Stored_Data[6]));  // open: Reset
  Memory _7 (
    .Clock(Clock), .WE(WE), .Din(Din[7]), .OE(OE), .Dout(Dout[7]), .Stored_Data(Stored_Data[7]));  // open: Reset
endmodule

module MAR (
  input  Clock,
  input  WE,
  input  [3:0] Din,
  input  OE,
  output [3:0] Dout,
  output [3:0] Stored_Data
);

  Memory _0 (
    .Clock(Clock), .WE(WE), .Din(Din[0]), .OE(OE), .Dout(Dout[0]), .Stored_Data(Stored_Data[0]));  // open: Reset
  Memory _1 (
    .Clock(Clock), .WE(WE), .Din(Din[1]), .OE(OE), .Dout(Dout[1]), .Stored_Data(Stored_Data[1]));  // open: Reset
  Memory _2 (
    .Clock(Clock), .WE(WE), .Din(Din[2]), .OE(OE), .Dout(Dout[2]), .Stored_Data(Stored_Data[2]));  // open: Reset
  Memory _3 (
    .Clock(Clock), .WE(WE), .Din(Din[3]), .OE(OE), .Dout(Dout[3]), .Stored_Data(Stored_Data[3]));  // open: Reset
endmodule

module ALU (
  input  [7:0] Reg_A,
  input  [7:0] Reg_B,
  input  OE,
  output [7:0] Dout,
  output [7:0] ALU_Result,
  output Carry_Out
);

  Adder adder_1 (.a(Reg_A), .b(Reg_B), .out(ALU_Result), .cout(Carry_Out));  // open: cin
  assign Dout = OE ? ALU_Result : 8'bz;  // Controlled_Buffer controlled_buffer_1
endmodule

module Decimal_Decode (
  input  [7:0] Din,
  output [31:0] Dout
);

  ROM #(.dataWidth(32)) rom_1 (
    .addr(Din),
    .data({Dout[31:28], Dout[15:12], Dout[27:24], Dout[11:8], Dout[23:20], Dout[7:4], Dout[19:16], Dout[3:0]}));

  // Notes on the sheet:
  //   contents of rom_1 (hex, n*v repeats v):
  //   e7 21 cb 6b 2d 6e ee 23 ef 2f 21e7 2121 21cb 216b 212d 216e 21ee 2123 21ef 212f cbe7 cb21 cbcb cb6b
  //   cb2d cb6e cbee cb23 cbef cb2f 6be7 6b21 6bcb 6b6b 6b2d 6b6e 6bee 6b23 6bef 6b2f 2de7 2d21 2dcb 2d6b
  //   2d2d 2d6e 2dee 2d23 2def 2d2f 6ee7 6e21 6ecb 6e6b 6e2d 6e6e 6eee 6e23 6eef 6e2f eee7 ee21 eecb ee6b
  //   ee2d ee6e eeee ee23 eeef ee2f 23e7 2321 23cb 236b 232d 236e 23ee 2323 23ef 232f efe7 ef21 efcb ef6b
  //   ef2d ef6e efee ef23 efef ef2f 2fe7 2f21 2fcb 2f6b 2f2d 2f6e 2fee 2f23 2fef 2f2f 21e7e7 21e721 21e7cb
  //   21e76b 21e72d 21e76e 21e7ee 21e723 21e7ef 21e72f 2121e7 212121 2121cb 21216b 21212d 21216e 2121ee
  //   212123 2121ef 21212f 21cbe7 21cb21 21cbcb 21cb6b 21cb2d 21cb6e 21cbee 21cb23 21cbef 21cb2f 216be7
  //   216b21 216bcb 216b6b 216b2d 216b6e 216bee 216b23 216bef 216b2f 212de7 212d21 212dcb 212d6b 212d2d
  //   212d6e 212dee 212d23 212def 212d2f 216ee7 216e21 216ecb 216e6b 216e2d 216e6e 216eee 216e23 216eef
  //   216e2f 21eee7 21ee21 21eecb 21ee6b 21ee2d 21ee6e 21eeee 21ee23 21eeef 21ee2f 2123e7 212321 2123cb
  //   21236b 21232d 21236e 2123ee 212323 2123ef 21232f 21efe7 21ef21 21efcb 21ef6b 21ef2d 21ef6e 21efee
  //   21ef23 21efef 21ef2f 212fe7 212f21 212fcb 212f6b 212f2d 212f6e 212fee 212f23 212fef 212f2f cbe7e7
  //   cbe721 cbe7cb cbe76b cbe72d cbe76e cbe7ee cbe723 cbe7ef cbe72f cb21e7 cb2121 cb21cb cb216b cb212d
  //   cb216e cb21ee cb2123 cb21ef cb212f cbcbe7 cbcb21 cbcbcb cbcb6b cbcb2d cbcb6e cbcbee cbcb23 cbcbef
  //   cbcb2f cb6be7 cb6b21 cb6bcb cb6b6b cb6b2d cb6b6e cb6bee cb6b23 cb6bef cb6b2f cb2de7 cb2d21 cb2dcb
  //   cb2d6b cb2d2d cb2d6e cb2dee cb2d23 cb2def cb2d2f cb6ee7 cb6e21 cb6ecb cb6e6b cb6e2d cb6e6e
  //   Decimal_Decoder
endmodule
